# Fritzing sketch beaglecam-prototype (saved by Fritzing 0.9.5d)
breadboards: 1

parts:
  BeagleBone1 = BeagleBone Black
  Camera_Module = TRANSCHIPTC5747 [package=camera_sfv24r-2st_2]
  16x2_I2C_Alphanumeric_LCD = LCD1602-I2C
  Arduino_Nano_33_BLE = Arduino Nano 33 BLE Sense
  PRU_Diag_LED = smd LED [color="Orange (620nm)" package="0805 [SMD]"]
  R1 = Resistor [tolerance=±5% resistance=470 package=THT]

nets:
  GND: BeagleBone1.P9_1_-_GND, Camera_Module.DOUT_5, 16x2_I2C_Alphanumeric_LCD.GND, Arduino_Nano_33_BLE.GND, Arduino_Nano_33_BLE.A7, R1.Pin_0
  N1: BeagleBone1.P9_3_-_3.3V, Camera_Module.DOUT_6
  N2: BeagleBone1.P9_10_-_Reset_button, Arduino_Nano_33_BLE.D2
  N3: BeagleBone1.P9_13_-_GPIO0_31/UART4-TX(6), Arduino_Nano_33_BLE.D4
  N4: BeagleBone1.P9_21_-_GPIO0_3/SPI0-D0(0)/UART2-TX(1), Camera_Module.DOUT_7
  N5: BeagleBone1.P9_22_-_GPIO0_3/SPI0-SCLK(0)/UART2-RX(1), Camera_Module.DOUT_4
  N6: BeagleBone1.P9_24_-_GPIO0_12/UART1-TX(0)/I2C1-SCL(3), Camera_Module.DOUT_3
  N7: BeagleBone1.P9_25_-_GPIO3_21, Camera_Module.PS1
  N8: BeagleBone1.P9_27_-_GPIO3_19, Camera_Module.CLK_IN
  N9: BeagleBone1.P9_29_-_GPIO3_15/SPI1-D0(3)/PWM0B(1), Camera_Module.RESET_N
  N10: BeagleBone1.P9_30_-_GPIO3_16/SPI1-D1(3), Camera_Module.PS2
  N11: BeagleBone1.P9_31_-_GPIO3_14/SPI1-SCLK(3)/PWM0A(1), Camera_Module.AVDD28
  N12: BeagleBone1.P9_41_-_GPIO0_20, Camera_Module.AGND
  N13: BeagleBone1.P9_42_-_GPIO0_7, Camera_Module.SHIELD
  N14: BeagleBone1.P8_7_-_GPIO2_2, Camera_Module.DOUT_2
  N15: BeagleBone1.P8_15_-_GPIO1_15, Camera_Module.VCLK_OUT
  N16: BeagleBone1.P8_16_-_GPIO1_14, Camera_Module.SDIN
  N17: BeagleBone1.P8_20_-_GPIO1_31, PRU_Diag_LED.anode
  N18: BeagleBone1.P8_21_-_GPIO1_30, Camera_Module.DOUT_8
  VCC: 16x2_I2C_Alphanumeric_LCD.VCC, Arduino_Nano_33_BLE.3V3
  N19: 16x2_I2C_Alphanumeric_LCD.SDA, Arduino_Nano_33_BLE.A4
  N20: 16x2_I2C_Alphanumeric_LCD.SCL, Arduino_Nano_33_BLE.A5
  N21: Arduino_Nano_33_BLE.D11/MOSI, Arduino_Nano_33_BLE.+5V
  N22: PRU_Diag_LED.cathode, R1.Pin_1

custom parts:
  BeagleBone Black: BeagleBone Black rev. A5B
  LCD1602-I2C: A standard character display, usually with 2x16 characters. Comes in many colors with LCM1602 IIC attached.
  Arduino Nano 33 BLE Sense: The Nano 33 BLE Sense (without headers) is Arduino’s 3.3V AI enabled board in the smallest available form factor: 45x18mm! The Arduino Nano 33 BLE Sense is a completely new board on a well-known form factor. It comes with a series of embedded sensors: 9 axis inertial sensor: what makes this board ideal for wearable devices humidity, and temperature sensor: to get highly accurate measurements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
